# Fritzing sketch Layout (saved by Fritzing 0.5.1b)
breadboards: 2

parts:
  B1 = 74HC595 [package="DIP16 [THT]"]
  CH1 = NPN-Transistor [package="TO92 [THT]"]
  B2 = 74HC595 [package="DIP16 [THT]"]
  B3 = 74HC595 [package="DIP16 [THT]"]
  B4 = 74HC595 [package="DIP16 [THT]"]
  B0 = 74HC595 [package="DIP16 [THT]"]
  CH0 = NPN-Transistor [package="TO92 [THT]"]
  CH2 = NPN-Transistor [package="TO92 [THT]"]
  CH3 = NPN-Transistor [package="TO92 [THT]"]
  CH5 = NPN-Transistor [package="TO92 [THT]"]
  CH6 = NPN-Transistor [package="TO92 [THT]"]
  CH4 = NPN-Transistor [package="TO92 [THT]"]
  CH7 = NPN-Transistor [package="TO92 [THT]"]
  R1 = Resistor [resistance=1k package=THT]
  R1_2 = Resistor [resistance=1k package=THT]
  R1_3 = Resistor [resistance=1k package=THT]
  R1_4 = Resistor [resistance=1k package=THT]
  R1_5 = Resistor [resistance=1k package=THT]
  R1_6 = Resistor [resistance=1k package=THT]
  R1_7 = Resistor [resistance=1k package=THT]
  R1_8 = Resistor [resistance=1k package=THT]
  Arduino1 = Arduino
  C1 = Ceramic Capacitor [capacitance=100nF rated_voltage=35V package="100 mil [THT, multilayer]"]  # not connected

nets:
  GND: B1.GND, B1.OE, B2.GND, B2.OE, B3.GND, B3.OE, B4.GND, B4.OE, B0.GND, B0.OE, Arduino1.GND
  N1: B1.Q7', B2.DS
  VCC: B1.MR, B1.VCC, CH1.C, B2.MR, B2.VCC, B3.MR, B3.VCC, B4.MR, B4.VCC, B0.MR, B0.VCC, CH0.C, CH2.C, CH3.C, CH5.C, CH6.C, CH4.C, CH7.C, Arduino1.+5V
  N2: B1.SH_CP, B2.SH_CP, B3.SH_CP, B4.SH_CP, B0.SH_CP, Arduino1.A2
  N3: B1.ST_CP, B2.ST_CP, B3.ST_CP, B4.ST_CP, B0.ST_CP, Arduino1.A1
  N4: B1.DS, Arduino1.A0
  N5: CH1.E, R1_2.Pin_0
  N6: CH1.B, B0.Q1
  N7: B2.Q7', B3.DS
  N8: B3.Q7', B4.DS
  N9: B4.Q7', B0.DS
  N10: B0.Q2, CH2.B
  N11: B0.Q3, CH3.B
  N12: B0.Q4, CH4.B
  N13: B0.Q5, CH5.B
  N14: B0.Q6, CH6.B
  N15: B0.Q7, CH7.B
  N16: B0.Q0, CH0.B
  N17: CH0.E, R1.Pin_0
  N18: CH2.E, R1_3.Pin_0
  N19: CH3.E, R1_4.Pin_0
  N20: CH5.E, R1_6.Pin_0
  N21: CH6.E, R1_7.Pin_0
  N22: CH4.E, R1_5.Pin_0
  N23: CH7.E, R1_8.Pin_0
