# Fritzing sketch 1cm_setup (saved by Fritzing 0.6.4b)
breadboards: 1

parts:
  7_Segment1 = 7 Segment Display
  7_Segment2 = 7 Segment Display
  J2 = female pin header, 11 pins [form="♀ (female)"]
  7_Segment3 = 7 Segment Display
  7_Segment4 = 7 Segment Display
  7_Segment5 = 7 Segment Display  # not connected

nets:
  N1: 7_Segment1.Segment_E, 7_Segment2.Segment_E, J2.pin5, 7_Segment3.Segment_E, 7_Segment4.Segment_E
  N2: 7_Segment1.Segment_D, 7_Segment2.Segment_D, J2.pin4, 7_Segment3.Segment_D, 7_Segment4.Segment_D
  N3: 7_Segment1.Segment_C, 7_Segment2.Segment_C, J2.pin3, 7_Segment3.Segment_C, 7_Segment4.Segment_C
  N4: 7_Segment1.Segment_B, 7_Segment2.Segment_B, J2.pin2, 7_Segment3.Segment_B, 7_Segment4.Segment_B
  N5: 7_Segment1.Segment_A, 7_Segment2.Segment_A, J2.pin1, 7_Segment3.Segment_A, 7_Segment4.Segment_A
  N6: 7_Segment1.Segment_F, 7_Segment2.Segment_F, J2.pin6, 7_Segment3.Segment_F, 7_Segment4.Segment_F
  N7: 7_Segment1.Segment_G, 7_Segment2.Segment_G, J2.pin7, 7_Segment3.Segment_G, 7_Segment4.Segment_G
