# Fritzing sketch 7seg-big-exp-pcb (saved by Fritzing 0.6.4b)
breadboards: 1

parts:
  74HC595 = 74HC595 [package="DIP16 [THT]"]
  UNL2003 = ULN2003A [package="DIP16 [THT]"]
  R1 = Resistor [tolerance=±5% resistance=220 package=THT]
  R2 = Resistor [tolerance=±5% resistance=220 package=THT]
  R3 = Resistor [tolerance=±5% resistance=220 package=THT]
  R4 = Resistor [tolerance=±5% resistance=220 package=THT]
  R5 = Resistor [tolerance=±5% resistance=220 package=THT]
  R6 = Resistor [tolerance=±5% resistance=220 package=THT]
  J4 = Generic_male_header___6_pins [form="♂ (male)"]
  74HC595_2 = 74HC595 [package="DIP16 [THT]"]

nets:
  N1: 74HC595.Q1, UNL2003.In_7
  N2: 74HC595.Q2, UNL2003.In_6
  N3: 74HC595.Q3, UNL2003.In_5
  N4: 74HC595.Q4, UNL2003.In_4
  N5: 74HC595.Q5, UNL2003.In_3
  N6: 74HC595.Q6, UNL2003.In_2
  N7: 74HC595.Q7, UNL2003.In_1
  GND: 74HC595.GND, 74HC595.OE, UNL2003.0V, J4.connector3, 74HC595_2.GND, 74HC595_2.OE
  N8: 74HC595.Q7', 74HC595_2.DS
  VCC: 74HC595.MR, 74HC595.VCC, J4.connector0, 74HC595_2.MR, 74HC595_2.VCC
  N9: 74HC595.SH_CP, J4.connector5, 74HC595_2.SH_CP
  N10: 74HC595.ST_CP, J4.connector4, 74HC595_2.ST_CP
  N11: 74HC595.DS, J4.connector2
  N12: R1.Pin_1, 74HC595_2.Q6
  N13: R2.Pin_1, 74HC595_2.Q5
  N14: R3.Pin_1, 74HC595_2.Q4
  N15: R4.Pin_1, 74HC595_2.Q3
  N16: R5.Pin_1, 74HC595_2.Q2
  N17: R6.Pin_1, 74HC595_2.Q1
