# Fritzing sketch MAX (saved by Fritzing 0.6.4b)
breadboards: 2

parts:
  DIG0 = 7 Segment Display
  DIG1 = 7 Segment Display
  DIG2 = 7 Segment Display
  DIG3 = 7 Segment Display
  DIG5 = 7 Segment Display
  MAX7219CNG1 = DIP___24_pins [part_number=MAX7219CNG chip_label=MAX7219CNG spacing=300mil]
  DIG4 = 7 Segment Display

nets:
  N1: DIG0.Segment_E, DIG1.Segment_E, DIG2.Segment_E, DIG3.Segment_E, DIG5.Segment_E, MAX7219CNG1.connector20, DIG4.Segment_E
  N2: DIG0.Segment_D, DIG1.Segment_D, DIG2.Segment_D, DIG3.Segment_D, DIG5.Segment_D, MAX7219CNG1.connector22, DIG4.Segment_D
  N3: DIG0.Segment_C, DIG1.Segment_C, DIG2.Segment_C, DIG3.Segment_C, DIG5.Segment_C, MAX7219CNG1.connector19, DIG4.Segment_C
  N4: DIG0.Segment_DP, DIG1.Segment_DP, DIG2.Segment_DP, DIG3.Segment_DP, DIG5.Segment_DP, MAX7219CNG1.connector21, DIG4.Segment_DP
  N5: DIG0.Segment_B, DIG1.Segment_B, DIG2.Segment_B, DIG3.Segment_B, DIG5.Segment_B, MAX7219CNG1.connector15, DIG4.Segment_B
  N6: DIG0.Segment_A, DIG1.Segment_A, DIG2.Segment_A, DIG3.Segment_A, DIG5.Segment_A, MAX7219CNG1.connector13, DIG4.Segment_A
  N7: DIG0.Segment_F, DIG1.Segment_F, DIG2.Segment_F, DIG3.Segment_F, DIG5.Segment_F, MAX7219CNG1.connector14, DIG4.Segment_F
  N8: DIG0.Segment_G, DIG1.Segment_G, DIG2.Segment_G, DIG3.Segment_G, DIG5.Segment_G, MAX7219CNG1.connector16, DIG4.Segment_G
