# Fritzing sketch OnExpBoard (saved by Fritzing 0.6.4b)
stripboards: 1

parts:
  U1 = 74HC595 [package="DIP16 [THT]"]
  J1 = Generic_male_header___6_pins [form="♂ (male)"]
  J2 = Generic_male_header___6_pins [form="♂ (male)"]
  IC1 = ULN2003A [package="DIP16 [THT]"]
  R1 = Resistor [tolerance=±5% resistance=220 package=THT]
  R2 = Resistor [tolerance=±5% resistance=220 package=THT]
  R3 = Resistor [tolerance=±5% resistance=220 package=THT]
  R4 = Resistor [tolerance=±5% resistance=220 package=THT]
  R5 = Resistor [tolerance=±5% resistance=220 package=THT]
  R6 = Resistor [tolerance=±5% resistance=220 package=THT]
  R7 = Resistor [tolerance=±5% resistance=220 package=THT]
  7_Segment1 = 7 Segment Display

nets:
  N1: U1.Q1, IC1.In_6
  N2: U1.Q2, IC1.In_5
  N3: U1.Q3, IC1.In_4
  N4: U1.Q4, IC1.In_3
  N5: U1.Q5, IC1.In_2
  N6: U1.Q6, IC1.In_1
  N7: U1.GND, U1.OE, J1.connector3, J2.connector3, IC1.0V
  N8: U1.Q7', J2.connector2
  N9: U1.MR, U1.VCC, J1.connector0, J2.connector0
  N10: U1.SH_CP, J1.connector5, J2.connector5
  N11: U1.ST_CP, J1.connector4, J2.connector4
  N12: U1.DS, J1.connector2
  N13: U1.Q0, IC1.In_7
  N14: J1.connector1, J2.connector1, IC1.COM_-_Common, 7_Segment1.common_anode
  N15: IC1.Out_7, R1.Pin_1
  N16: IC1.Out_6, R2.Pin_1
  N17: IC1.Out_5, R4.Pin_1
  N18: IC1.Out_4, R3.Pin_1
  N19: IC1.Out_3, R5.Pin_1
  N20: IC1.Out_2, R6.Pin_1
  N21: IC1.Out_1, R7.Pin_1
  N22: R1.Pin_0, 7_Segment1.Segment_A
  N23: R2.Pin_0, 7_Segment1.Segment_B
  N24: R3.Pin_0, 7_Segment1.Segment_D
  N25: R4.Pin_0, 7_Segment1.Segment_C
  N26: R5.Pin_0, 7_Segment1.Segment_E
  N27: R6.Pin_0, 7_Segment1.Segment_F
  N28: R7.Pin_0, 7_Segment1.Segment_G
